# Fritzing sketch SkinnerBox (saved by Fritzing 0.8.7b)
circuit board: 8.46667cm x 5.64444cm
breadboards: 1

parts:
  IC1 = ULN2803A [package=THT]
  M1 = Stepper Motor - Unipolar
  J1 = Piezo Speaker
  S1 = SWITCH-MOMENTARY-2 [package=tactile-switch-1101ne]
  R1 = 1K Ω Resistor [package=THT]
  R2 = 10K Ω Resistor [package=THT]
  Raspberry_Pi_B_rev1 = Raspberry Pi B rev2

nets:
  N1: IC1.In_1, Raspberry_Pi_B_rev1.GPIO_18
  N2: IC1.In_2, Raspberry_Pi_B_rev1.GPIO_22
  N3: IC1.In_3, Raspberry_Pi_B_rev1.GPIO_23
  N4: IC1.In_4, Raspberry_Pi_B_rev1.GPIO_24
  N5: IC1.0V, M1.COMMON_1, M1.COMMON_2, Raspberry_Pi_B_rev1.5V
  N6: IC1.COM_-_Common, J1.pin1, S1.2, Raspberry_Pi_B_rev1.GND
  N7: IC1.Out_4, M1.D
  N8: IC1.Out_3, M1.B
  N9: IC1.Out_2, M1.C
  N10: IC1.Out_1, M1.A
  N11: J1.pin2, Raspberry_Pi_B_rev1.GPIO_4
  N12: S1.1, R1.Pin_1, R2.Pin_1
  N13: R1.Pin_0, Raspberry_Pi_B_rev1.GPIO_25
  N14: R2.Pin_0, Raspberry_Pi_B_rev1.3V3

custom parts:
  1K Ω Resistor: A generic resistor (0.25W)
  10K Ω Resistor: A generic resistor (0.25W)
